# Fritzing sketch Wiring Diagram Wheater station Amin Moubariki (saved by Fritzing 0.9.3b)
breadboards: 1

parts:
  WeMos_D1_Mini1 = WeMos D1 Mini  # not connected
  RHT1 = Humidity and Temperature Sensor RHT03
  S1 = Pushbutton [package="[THT]"]
  R1 = Resistor [tolerance=±5% resistance=220 package=THT]
  Display1 = LCD screen 16x2 IIC [part_number=101290]

nets:
  VCC: RHT1.Vcc, R1.Pin_1, Display1.VCC
  N1: RHT1.GND_2, S1.Pin_1, S1.Pin_2, Display1.GND
  N2: S1.Pin_3, S1.Pin_4, R1.Pin_0

custom parts:
  LCD screen 16x2 IIC: LCD screen with HD44780 controller enables showing text, symbols, value or anything else that comes from Croduino/Arduino. It is capable of showing 16 symbols in two lines and therefore can be used in many projects that need to send clearly visible and legible output information.. • Color of symbols: White • Backlight: Blue • Dimensions: 80 x 36 x 12 mm • Screen dimensions: 64.5 x 16 mm •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
