# Fritzing sketch wiring_diagram_updated (saved by Fritzing 0.9.3b)
breadboards: 1

parts:
  WeMos_D1_Mini1 = WeMos D1 Mini  # not connected
  S1 = Pushbutton [package="[THT]"]
  R1 = Resistor [tolerance=±5% resistance=220 package=THT]
  LCM1602_IIC1 = LCM1602 IIC [part_number="LCM1602 IIC" chip_label="LCM1602 IIC" package="DIP (Dual Inline) [THT]"]
  LCD1 = LCD screen
  Mod1 = KY-015 Temperature & Humidity Sensor Module [package="Breakout board"]
  USBTTL1 = Micro USB B Plug  # not connected

nets:
  N1: S1.Pin_1, S1.Pin_2, LCM1602_IIC1.GND, Mod1.-
  N2: S1.Pin_3, S1.Pin_4, R1.Pin_0
  N3: R1.Pin_1, LCM1602_IIC1.VCC, Mod1.S
  VSS: LCM1602_IIC1.VSS, LCD1.VSS
  VDD: LCM1602_IIC1.VDD, LCD1.VDD
  N4: LCM1602_IIC1.V0, LCD1.V0
  N5: LCM1602_IIC1.RS, LCD1.RS
  N6: LCM1602_IIC1.RW, LCD1.R/W
  N7: LCM1602_IIC1.E, LCD1.E
  N8: LCM1602_IIC1.D0, LCD1.DB0
  N9: LCM1602_IIC1.D1, LCD1.DB1
  N10: LCM1602_IIC1.D2, LCD1.DB2
  N11: LCM1602_IIC1.D3, LCD1.DB3
  N12: LCM1602_IIC1.D4, LCD1.DB4
  N13: LCM1602_IIC1.D5, LCD1.DB5
  N14: LCM1602_IIC1.D6, LCD1.DB6
  N15: LCM1602_IIC1.D7, LCD1.DB7
  N16: LCM1602_IIC1.A, LCD1.LED+
  N17: LCM1602_IIC1.K, LCD1.LED-

notes:
  Power source

custom parts:
  LCM1602 IIC: I2C-Module to use a 1602 or 2004 LCD on with the wire.h libory Serial LCD Modul
  KY-015 Temperature & Humidity Sensor Module: KY-015 temperature and humidity sensor module, provides a low-latency serial interface to measure humidity and temperature.
